# Fritzing sketch nrf_jammer_fritzing (saved by Fritzing 0.9.4)
circuit board: 7.91cm x 6cm

parts:
  M1 = STM32F103C8T6 blue mini board
  Part1 = NRF24L01+ Breakout Board
  Part2 = NRF24L01+ Breakout Board
  Part3 = NRF24L01+ Breakout Board

nets:
  GND: M1.G, M1.GND, Part1.GND, Part2.GND, Part3.GND
  N1: M1.A0, Part1.CE
  N2: M1.A1, Part1.CS
  N3: M1.A2, Part2.CE
  N4: M1.A3, Part2.CS
  N5: M1.A5, Part1.SCK, Part2.SCK, Part3.SCK
  N6: M1.A6, Part1.MISO, Part2.MISO, Part3.MISO
  N7: M1.A7, Part1.MOSI, Part2.MOSI, Part3.MOSI
  N8: M1.B0, Part3.CE
  N9: M1.B1, Part3.CS
  VCC: M1.3.3V, M1.3.3, Part1.VCC, Part2.VCC, Part3.VCC
